// Logisim project traffic light system_2nd semester project.circ as structural Verilog: 5 circuits, main circuit main
module main (
  input  in_1
);

  wire _0_5_COUNTER____2_BIT_COUNTER__2_4_MUX_out_2, _0_5_COUNTER____2_BIT_COUNTER__2_4_MUX_out_3,
       _0_5_COUNTER____2_BIT_COUNTER__2_4_MUX_out_4, _0_5_COUNTER____2_BIT_COUNTER__2_4_MUX_out_5,
       d_flipflop_1_out_2, d_flipflop_1_out_3, d_flipflop_1_out_4, d_flipflop_2_out_2, d_flipflop_2_out_3,
       d_flipflop_2_out_4, D_FLIPFLOP_3_out_2, D_FLIPFLOP_3_out_3, D_FLIPFLOP_3_out_4, d_flipflop_4_out_2,
       d_flipflop_4_out_3, d_flipflop_4_out_4;

  starting_part _0_5_COUNTER____2_BIT_COUNTER__2_4_MUX (
    .in_1(in_1), .out_2(_0_5_COUNTER____2_BIT_COUNTER__2_4_MUX_out_2),
    .out_3(_0_5_COUNTER____2_BIT_COUNTER__2_4_MUX_out_3),
    .out_4(_0_5_COUNTER____2_BIT_COUNTER__2_4_MUX_out_4), .out_5(_0_5_COUNTER____2_BIT_COUNTER__2_4_MUX_out_5));
  d_flipflop d_flipflop_1 (
    .in_1(_0_5_COUNTER____2_BIT_COUNTER__2_4_MUX_out_5), .out_2(d_flipflop_1_out_2),
    .out_3(d_flipflop_1_out_3), .out_4(d_flipflop_1_out_4));
  LED led_1 (.in(d_flipflop_1_out_3));
  LED led_2 (.in(d_flipflop_1_out_2));
  LED led_3 (.in(d_flipflop_1_out_4));
  LED led_4 (.in(d_flipflop_2_out_4));
  LED led_5 (.in(d_flipflop_2_out_3));
  LED led_6 (.in(d_flipflop_2_out_2));
  d_flipflop d_flipflop_2 (
    .in_1(_0_5_COUNTER____2_BIT_COUNTER__2_4_MUX_out_4), .out_2(d_flipflop_2_out_2),
    .out_3(d_flipflop_2_out_3), .out_4(d_flipflop_2_out_4));
  LED led_7 (.in(D_FLIPFLOP_3_out_2));
  LED led_8 (.in(D_FLIPFLOP_3_out_3));
  d_flipflop D_FLIPFLOP_3 (
    .in_1(_0_5_COUNTER____2_BIT_COUNTER__2_4_MUX_out_2), .out_2(D_FLIPFLOP_3_out_2),
    .out_3(D_FLIPFLOP_3_out_3), .out_4(D_FLIPFLOP_3_out_4));
  LED led_9 (.in(D_FLIPFLOP_3_out_4));
  LED led_10 (.in(d_flipflop_4_out_4));
  d_flipflop d_flipflop_4 (
    .in_1(_0_5_COUNTER____2_BIT_COUNTER__2_4_MUX_out_3), .out_2(d_flipflop_4_out_2),
    .out_3(d_flipflop_4_out_3), .out_4(d_flipflop_4_out_4));
  LED led_11 (.in(d_flipflop_4_out_3));
  LED led_12 (.in(d_flipflop_4_out_2));
endmodule

module d_flipflop (
  input  in_1,
  output out_2,
  output out_3,
  output out_4
);

  wire and_1_out, and_2_out, and_3_out, and_4_out, and_5_out, and_6_out, and_7_out, and_8_out, and_9_out,
       clock_1_out, d_ff_1_q, d_ff_2_q, d_ff_3_q, nor_1_out, not_1_out, not_2_out, not_3_out, not_4_out,
       not_5_out, not_6_out, or_1_out, or_2_out, or_3_out;

  Clock clock_1 (.out(clock_1_out));
  and and_1 (and_1_out, not_3_out, d_ff_2_q, d_ff_3_q);
  and and_2 (and_2_out, d_ff_1_q, not_1_out, not_2_out);
  and and_3 (and_3_out, not_3_out, not_1_out, d_ff_3_q);
  and and_4 (and_4_out, not_3_out, d_ff_2_q, not_2_out);
  and and_5 (and_5_out, not_3_out, d_ff_2_q, not_2_out);
  and and_6 (and_6_out, d_ff_1_q, not_1_out, not_2_out);
  and and_7 (and_7_out, not_3_out, not_2_out, in_1);
  or or_1 (or_1_out, and_1_out, and_2_out);
  or or_2 (or_2_out, and_3_out, and_4_out);
  or or_3 (or_3_out, and_5_out, and_6_out, and_7_out);
  not not_1 (not_1_out, d_ff_2_q);
  not not_2 (not_2_out, d_ff_3_q);
  D_Flip_Flop d_ff_1 (.clk(clock_1_out), .D(or_1_out), .Q(d_ff_1_q));  // open: Qn, preset, en, reset
  D_Flip_Flop d_ff_2 (.clk(clock_1_out), .D(or_2_out), .Q(d_ff_2_q));  // open: Qn, preset, en, reset
  D_Flip_Flop d_ff_3 (.clk(clock_1_out), .D(or_3_out), .Q(d_ff_3_q));  // open: Qn, preset, en, reset
  not not_3 (not_3_out, d_ff_1_q);
  not not_4 (not_4_out, d_ff_1_q);
  not not_5 (not_5_out, d_ff_2_q);
  not not_6 (not_6_out, d_ff_2_q);
  nor nor_1 (nor_1_out, d_ff_1_q, d_ff_2_q, d_ff_3_q);
  and and_8 (and_8_out, not_4_out, not_5_out, d_ff_3_q);
  and and_9 (and_9_out, d_ff_1_q, not_6_out, d_ff_3_q);
  or or_4 (out_2, nor_1_out, and_8_out);
  or or_5 (out_3, and_8_out, and_9_out);
  nor nor_2 (out_4, out_2, out_3);
endmodule

module starting_part (
  input  in_1,
  output out_2,
  output out_3,
  output out_4,
  output out_5
);

  wire and_1_out, and_2_out, clock_1_out, clock_2_out, j_k_ff_1_q, j_k_ff_1_qn, j_k_ff_2_q, j_k_ff_2_qn,
       j_k_ff_3_q, j_k_ff_3_qn, j_k_ff_4_q, j_k_ff_5_q, not_1_out, not_2_out, not_3_out, not_4_out,
       not_5_out, not_6_out;

  Clock clock_1 (.out(clock_1_out));
  not not_1 (not_1_out, in_1);
  J_K_Flip_Flop j_k_ff_1 (
    .J(not_1_out), .clk(clock_1_out), .K(not_1_out), .Q(j_k_ff_1_q), .Qn(j_k_ff_1_qn), .reset(and_1_out));  // open: preset, en
  Clock clock_2 (.out(clock_2_out));
  not not_2 (not_2_out, j_k_ff_1_q);
  J_K_Flip_Flop j_k_ff_2 (
    .J(not_1_out), .clk(j_k_ff_1_qn), .K(not_1_out), .Q(j_k_ff_2_q), .Qn(j_k_ff_2_qn), .reset(and_1_out));  // open: preset, en
  J_K_Flip_Flop j_k_ff_3 (
    .J(and_2_out), .clk(clock_2_out), .K(and_2_out), .Q(j_k_ff_3_q), .Qn(j_k_ff_3_qn));  // open: preset, en, reset
  J_K_Flip_Flop j_k_ff_4 (
    .J(not_1_out), .clk(j_k_ff_2_qn), .K(not_1_out), .Q(j_k_ff_4_q), .reset(and_1_out));  // open: Qn, preset, en
  and and_1 (and_1_out, j_k_ff_4_q, j_k_ff_2_q, not_2_out);
  J_K_Flip_Flop j_k_ff_5 (
    .J(and_2_out), .clk(j_k_ff_3_qn), .K(and_2_out), .Q(j_k_ff_5_q));  // open: Qn, preset, en, reset
  and and_2 (and_2_out, j_k_ff_4_q, j_k_ff_1_q);
  not not_3 (not_3_out, j_k_ff_5_q);
  not not_4 (not_4_out, j_k_ff_3_q);
  not not_5 (not_5_out, j_k_ff_5_q);
  not not_6 (not_6_out, j_k_ff_3_q);
  and and_3 (out_3, not_5_out, j_k_ff_3_q);
  and and_4 (out_4, j_k_ff_5_q, not_6_out);
  and and_5 (out_5, j_k_ff_5_q, j_k_ff_3_q);
  and and_6 (out_2, not_3_out, not_4_out);

  // Notes on the sheet:
  //   2 BIT COUNTER
  //   0-5 COUNTER
  //   2-4 MULTIPLEXER
endmodule

module _2_4_mux (
  input  A,
  input  b,
  output out_3,
  output out_4,
  output out_5,
  output out_6
);

  wire not_1_out, not_2_out, not_3_out, not_4_out;

  not not_1 (not_1_out, A);
  not not_2 (not_2_out, b);
  not not_3 (not_3_out, A);
  not not_4 (not_4_out, b);
  and and_1 (out_3, not_1_out, not_2_out);
  and and_2 (out_4, not_3_out, b);
  and and_3 (out_5, A, not_4_out);
  and and_4 (out_6, A, b);
endmodule

module _2_bit_counter (
  input  in_1,
  output out_2,
  output out_3
);

  wire clock_1_out, j_k_ff_1_qn, undriven;

  Clock clock_1 (.out(clock_1_out));
  J_K_Flip_Flop j_k_ff_1 (
    .J(undriven), .clk(clock_1_out), .K(undriven), .Q(out_3), .Qn(j_k_ff_1_qn));  // open: preset, en, reset
  J_K_Flip_Flop j_k_ff_2 (.J(undriven), .clk(j_k_ff_1_qn), .K(undriven), .Q(out_2));  // open: Qn, preset, en, reset
endmodule
